# Fritzing sketch HU Miniproject CSN (saved by Fritzing 0.9.3b)
breadboards: 2

parts:
  LED1 = LED - 5mm [color="Red (633nm)" package="5 mm [THT]"]
  R1 = Resistor [tolerance=±5% resistance=1k package=THT]
  LED2 = LED - 5mm [color="Blue (430nm)" package="5 mm [THT]"]
  R2 = Resistor [tolerance=±5% resistance=1k package=THT]
  Raspberry_Pi_1 = Raspberry Pi 3 [part_number=RPI-3-V1.2]
  M1 = fc-51 [package=THT]
  Part1 = KY-008 Laser Transmitter Module [package="Breakout board"]
  S1 = Pushbutton [package="[THT]"]
  R4 = Resistor [tolerance=±5% resistance=1k package=THT]
  Raspberry_Pi_2 = Raspberry Pi 3 [part_number=RPI-3-V1.2]
  LED3 = LED - 5mm [color="Blue (430nm)" package="5 mm [THT]"]
  LED4 = LED - 5mm [color="Red (633nm)" package="5 mm [THT]"]
  R5 = Resistor [tolerance=±5% resistance=1k package=THT]
  R6 = Resistor [tolerance=±5% resistance=1k package=THT]

nets:
  N1: LED1.cathode, R1.Pin_0
  N2: LED1.anode, Raspberry_Pi_1.GPIO5
  N3: R1.Pin_1, R2.Pin_1, Raspberry_Pi_1.GND, M1.pin2
  N4: LED2.cathode, R2.Pin_0
  N5: LED2.anode, Raspberry_Pi_1.GPIO6
  3V3: Raspberry_Pi_1.3v3, Raspberry_Pi_1.3V3, M1.pin3, R4.Pin_1
  N6: Raspberry_Pi_1.GPIO26, S1.Pin_1, S1.Pin_2
  N7: Raspberry_Pi_1.GPIO23, M1.pin1
  N8: Part1.S, Raspberry_Pi_2.GND, R5.Pin_1, R6.Pin_1
  N9: Part1.-, Raspberry_Pi_2.3v3
  N10: S1.Pin_3, S1.Pin_4, R4.Pin_0
  N11: Raspberry_Pi_2.GPIO5, LED4.anode
  N12: Raspberry_Pi_2.GPIO6, LED3.anode
  N13: LED3.cathode, R5.Pin_0
  N14: LED4.cathode, R6.Pin_0

notes:
  Server
  Client
  Light Sender
  Only one client has this
  Light Receiver
  Keypad (optional)

custom parts:
  KY-008 Laser Transmitter Module: Laser Transmitter module KY-008 for Arduino, emits a dot shaped red laser beam.
